// Logisim project HuuCao_HW5.circ as structural Verilog
module _1_bit_ALU (
  input  Sub_Add,
  input  Cin,
  input  [1:0] OPR,
  input  A,
  input  B,
  input  Less,
  output Result,
  output Cout,
  output Set
);

  wire and_1_out, multiplexer_1_out, not_1_out, or_1_out;

  not not_1 (not_1_out, B);
  Multiplexer #(.enable("false")) multiplexer_1 (.in0(B), .in1(not_1_out), .out(multiplexer_1_out), .sel(Sub_Add));
  and and_1 (and_1_out, A, B);
  or or_1 (or_1_out, A, B);
  Adder #(.width(1)) adder_1 (.a(A), .b(multiplexer_1_out), .out(Set), .cin(Cin), .cout(Cout));
  Multiplexer #(.select(2), .enable("false")) multiplexer_2 (
    .in0(and_1_out), .in1(or_1_out), .in2(Set), .in3(Less), .out(Result), .sel(OPR));
endmodule

module _8_bit_ALU (
  input  [7:0] A,
  input  Sub,
  input  [1:0] Op,
  input  [7:0] B,
  output [7:0] out_5,
  output Zero,
  output Cout
);

  wire n1_bit_alu_1_cout, n1_bit_alu_2_cout, n1_bit_alu_3_cout, n1_bit_alu_4_cout, n1_bit_alu_5_cout,
       n1_bit_alu_6_cout, n1_bit_alu_7_cout, n1_bit_alu_8_set;

  // Probe on A
  // Probe on B
  _1_bit_ALU u_1_bit_alu_1 (
    .A(A[0]), .B(B[0]), .Less(n1_bit_alu_8_set), .Result(out_5[0]), .Sub_Add(Sub), .Cin(Sub), .OPR(Op),
    .Cout(n1_bit_alu_1_cout));  // open: Set
  _1_bit_ALU u_1_bit_alu_2 (
    .A(A[1]), .B(B[1]), .Less(1'b0), .Result(out_5[1]), .Sub_Add(Sub), .Cin(n1_bit_alu_1_cout), .OPR(Op),
    .Cout(n1_bit_alu_2_cout));  // open: Set
  _1_bit_ALU u_1_bit_alu_3 (
    .A(A[2]), .B(B[2]), .Less(1'b0), .Result(out_5[2]), .Sub_Add(Sub), .Cin(n1_bit_alu_2_cout), .OPR(Op),
    .Cout(n1_bit_alu_3_cout));  // open: Set
  _1_bit_ALU u_1_bit_alu_4 (
    .A(A[3]), .B(B[3]), .Less(1'b0), .Result(out_5[3]), .Sub_Add(Sub), .Cin(n1_bit_alu_3_cout), .OPR(Op),
    .Cout(n1_bit_alu_4_cout));  // open: Set
  _1_bit_ALU u_1_bit_alu_5 (
    .A(A[4]), .B(B[4]), .Less(1'b0), .Result(out_5[4]), .Sub_Add(Sub), .Cin(n1_bit_alu_4_cout), .OPR(Op),
    .Cout(n1_bit_alu_5_cout));  // open: Set
  _1_bit_ALU u_1_bit_alu_6 (
    .A(A[5]), .B(B[5]), .Less(1'b0), .Result(out_5[5]), .Sub_Add(Sub), .Cin(n1_bit_alu_5_cout), .OPR(Op),
    .Cout(n1_bit_alu_6_cout));  // open: Set
  _1_bit_ALU u_1_bit_alu_7 (
    .A(A[6]), .B(B[6]), .Less(1'b0), .Result(out_5[6]), .Sub_Add(Sub), .Cin(n1_bit_alu_6_cout), .OPR(Op),
    .Cout(n1_bit_alu_7_cout));  // open: Set
  _1_bit_ALU u_1_bit_alu_8 (
    .A(A[7]), .B(B[7]), .Less(1'b0), .Result(out_5[7]), .Sub_Add(Sub), .Cin(n1_bit_alu_7_cout), .OPR(Op),
    .Cout(Cout), .Set(n1_bit_alu_8_set));
  // Probe on out_5
  nor nor_1 (Zero, out_5[0], out_5[1], out_5[2], out_5[3], out_5[4], out_5[5], out_5[6], out_5[7]);
endmodule

module multiplier_8_8 (
  input  [3:0] Multiplicand,
  input  [3:0] Multiplier,
  output [7:0] out_3
);

  wire CLK, clock_1_out, Iteration_Counter_carry, Multiplier_0;
  wire [2:0] Iteraion_no, Iteration_no;
  wire [7:0] bit_extender_1_out, bit_extender_2_out, multiplexer_1_out, multiplicand_shifted, Product_2_q,
       Product_q;
  wire [7:1] shifter_1_out;

  Clock clock_1 (.out(clock_1_out));
  // Probe on Multiplicand
  // Probe on Multiplier
  Clock clock_2 (.out(CLK));
  Counter #(.width(3), .max('h7)) Iteration_Counter (
    .Q(Iteration_no), .carry(Iteration_Counter_carry), .clk(clock_1_out));  // open: load, D, count, clr
  and and_1 (clock_1_out, CLK, Iteration_Counter_carry);
  assign bit_extender_1_out = {{4{1'b0}}, Multiplier};  // Bit_Extender bit_extender_1
  Shifter #(.shift("lr")) shifter_1 (
    .in(bit_extender_1_out), .\dist (Iteration_no), .out({shifter_1_out, Multiplier_0}));
  assign bit_extender_2_out = {{4{1'b0}}, Multiplicand};  // Bit_Extender bit_extender_2
  Shifter shifter_2 (.in(bit_extender_2_out), .\dist (Iteraion_no), .out(multiplicand_shifted));
  Register Product (.D(multiplexer_1_out), .Q(Product_q));  // open: en, clk, clr
  Multiplexer #(.width(8)) multiplexer_1 (
    .in0({8{1'b0}}), .in1(multiplicand_shifted), .out(multiplexer_1_out), .sel(Multiplier_0));  // open: en
  Register Product_2 (.D(out_3), .Q(Product_2_q), .clk(CLK));  // open: en, clr
  _8_bit_ALU u_8_bit_alu_1 (.A(Product_q), .B(Product_2_q), .out_5(out_3), .Sub(1'b0), .Op(2'b10));  // open: Zero, Cout
  // Probe on out_3

  // Other names for the same wires on the sheet: Product[7:0] = out_3
endmodule
